# Fritzing sketch ARDUINO_DUE (saved by Fritzing 0.9.3b)

parts:
  Arduino_Due1 = Arduino DUE
  M1 = fc-51 [package=THT]
  M2 = fc-51 [package=THT]
  M3 = fc-51 [package=THT]
  M4 = fc-51 [package=THT]
  M5 = fc-51 [package=THT]
  M6 = fc-51 [package=THT]
  M7 = fc-51 [package=THT]
  M8 = fc-51 [package=THT]
  M9 = fc-51 [package=THT]
  M10 = fc-51 [package=THT]
  J1 = Basic Servo
  J5 = Basic Servo
  J6 = Basic Servo
  J7 = Basic Servo
  J8 = Basic Servo
  M11 = fc-51 [package=THT]
  J9 = Basic Servo

nets:
  N1: Arduino_Due1.D8, J8.pulse
  N2: Arduino_Due1.D6, J9.pulse
  N3: Arduino_Due1.D24, J7.pulse
  N4: Arduino_Due1.D30, M1.pin1
  N5: Arduino_Due1.D32, M2.pin1
  N6: Arduino_Due1.D33, M10.pin1
  N7: Arduino_Due1.D34, M3.pin1
  N8: Arduino_Due1.D35, M11.pin1
  N9: Arduino_Due1.D38, J5.pulse
  N10: Arduino_Due1.D39, M7.pin1
  N11: Arduino_Due1.D41, J1.pulse
  N12: Arduino_Due1.D42, M4.pin1
  N13: Arduino_Due1.D43, M6.pin1
  N14: Arduino_Due1.D44, J6.pulse
  N15: Arduino_Due1.D45, M5.pin1
  N16: Arduino_Due1.D49, M8.pin1
  N17: Arduino_Due1.D53, M9.pin1

notes:
  ROOM 5 ROOM 6
  FRONT BACK
  ROOM 4 ROOM 4
  FRONT BACK
  ROOM 3 ROOM 3
  FRONT BACK
  ROOM 2 ROOM 2
  FRONT BACK
  ROOM 1 ROOM 1
  FRONT BACK
  Servo room 2
  Servo room 3
  Servo room 4
  Servo room 5
  Servo room 1
  ALL THE POSITIVE AND THE NEGATIVE SUPPLY COLURED EITHER RED AND BLACK OR BLUE AND WHITE. IT IS NOT SHOWN TO AVOID CLUMSINESS.
  Garage

custom parts:
  Arduino DUE: Arduino Due microcontroller. Breadboard based on photo taken from arduino.cc v1.1
