# Fritzing sketch Arduino UNO_main (saved by Fritzing 0.9.3b)

parts:
  Part1 = Arduino Uno (Rev3) - ICSP
  Part2 = RFID USB Reader
  J1 = Basic Servo

nets:
  N1: Part1.D9_PWM, Part2.CP
  N2: Part1.D10_PWM/SS, Part2.VCC
  N3: Part1.D11_PWM/MOSI, Part2.TX-O
  N4: Part1.D12/MISO, Part2.TX-O-RS232
  N5: Part1.D13/SCK, Part2.GND
  N6: Part1.GND, Part2.ANT2
  N7: Part1.D2, J1.pulse
  N8: Part1.3V3, Part2.GNDT
