# Fritzing sketch Arduino_UNO_Garage (saved by Fritzing 0.9.3b)

parts:
  J3 = Basic Servo
  Part2 = RFID USB Reader
  Part3 = Arduino Uno (Rev3) - ICSP
  J4 = Basic Servo
  J5 = Piezo Speaker
  hc-sr2 = hc-sr04

nets:
  N1: J3.pulse, Part3.D8
  N2: Part2.GNDT, Part3.D10_PWM/SS
  N3: Part2.CP, Part3.D13/SCK
  N4: Part2.ANT2, Part3.D11_PWM/MOSI
  N5: Part2.ANT1, Part3.D12/MISO
  GND: Part2.TX-O, Part3.GND, J5.pin1, hc-sr2.GND
  N6: Part2.GND, Part3.D9_PWM
  VCC: Part2.VCC, Part3.3V3
  N7: Part3.D4, hc-sr2.Echo
  N8: Part3.D5_PWM, hc-sr2.Trig
  N9: Part3.D7, J4.pulse
  5V: Part3.5V, J5.pin2, hc-sr2.VCC
