# Fritzing sketch fan_circuit (saved by Fritzing 0.9.3b)
breadboards: 1

parts:
  F1 = Fan - Ventilador [package=THT]
  Arduino_Due1 = Arduino DUE
  U1 = TRANSISTOR_NPN_2 [package=to-92]
  R1 = Resistor [tolerance=±5% resistance=220 package=THT]
  R2 = Resistor [tolerance=±5% resistance=220 package=THT]

nets:
  N1: F1.GND, U1.E
  N2: Arduino_Due1.GROUND, U1.C
  N3: Arduino_Due1.D22, R2.Pin_1
  N4: U1.B, R1.Pin_0
  N5: R1.Pin_1, R2.Pin_0

custom parts:
  Fan - Ventilador: Ventilador de 2 pines, se encuentra comunmente en computadoras de escritorio
  Arduino DUE: Arduino Due microcontroller. Breadboard based on photo taken from arduino.cc v1.1
